# Fritzing sketch fritzing_Design (saved by Fritzing 0.9.3b)
breadboards: 1

parts:
  GSM_SIM_GPSR_SMS_SIM900_SIM1 = SIM800L [package=THT]
  GY1 = MPU-6050 Board GY-521 [form="♀ (female)" package=THT]
  Part1 = u-blox NEO-6M GPS Breakout
  S1 = SPST Switch [package=switch-spdt_lock.007s]
  Part2 = Arduino Nano (Rev3.0)
  LED1 = smd LED [color="Green (560nm)" package="1206 [SMD]"]
  J1 = Piezo Speaker
  S2 = SPST Switch [package=switch-spdt_lock.007s]
  LED2 = smd LED [color="White (6500K)" package="1206 [SMD]"]

nets:
  5V: GSM_SIM_GPSR_SMS_SIM900_SIM1.5V, GY1.pin1, Part1.VCC, Part2.VIN
  N1: GSM_SIM_GPSR_SMS_SIM900_SIM1.SIM_TXD, Part2.D9
  N2: GSM_SIM_GPSR_SMS_SIM900_SIM1.SIM_RXD, Part2.D10
  GND: GSM_SIM_GPSR_SMS_SIM900_SIM1.GND, GY1.pin2, Part1.GND, S1.P, Part2.GND, LED1.cathode, J1.pin1, S2.P, LED2.cathode
  N3: GY1.pin3, Part2.A5
  N4: GY1.pin4, GY1.pin5, Part2.A4
  N5: Part1.TXD, Part2.D4
  N6: Part1.RXD, Part2.D3
  N7: S1.S, Part2.D8
  N8: Part2.D2, LED2.anode
  N9: Part2.D5, J1.pin2
  N10: Part2.D12/MISO, S2.S
  N11: Part2.D13/SCK, LED1.anode

custom parts:
  MPU-6050 Board GY-521: Acelerometro y Giroscopio MPU-6050 Board GY-521
